# Fritzing sketch SeguiLSol 2 (saved by Fritzing 0.9.1b)
breadboards: 1

parts:
  C2 = Capacitor Polarized [package=panasonic_g]
  M1 = Stepper Motor - Bipolar
  MD09B1 = A4988 Stepper Motor Driver Carrier
  Part1 = Arduino Uno (Rev3)
  R1 = Photocell (LDR) [package=THT]
  R2 = Resistor [tolerance=±5% resistance=10k package=THT]
  R3 = Photocell (LDR) [package=THT]
  R4 = Resistor [tolerance=±5% resistance=10k package=THT]
  R5 = Photocell (LDR) [package=THT]
  R6 = Photocell (LDR) [package=THT]
  R7 = Resistor [tolerance=±5% resistance=2.2k package=THT]
  R8 = Resistor [tolerance=±5% resistance=2.2k package=THT]
  R9 = Temperature Sensor (Thermistor) [thermistor_type=NTC package=THT]
  R10 = Temperature Sensor (Thermistor) [thermistor_type=NTC package=THT]
  R11 = Resistor [tolerance=±5% resistance=10k package=THT]  # not connected
  R12 = Resistor [tolerance=±5% resistance=10k package=THT]
  S1 = Pushbutton [package=THT]
  R13 = Resistor [tolerance=±5% resistance=10k package=THT]
  VCC1 = LC-R121R3P
  F1 = FUSE [package=fuse_5mm]

nets (from the breadboard view):
  N1: C2.+, MD09B1.VMOT, F1.1
  N2: C2.-, MD09B1.GROUND, Part1.GND, R2.Pin_1, R7.Pin_1, R12.Pin_1, R13.Pin_1, VCC1.pin2
  N3: M1.A, MD09B1.OUT_2A
  N4: M1.C, MD09B1.OUT_2B
  N5: M1.B, MD09B1.OUT_1A
  N6: M1.D, MD09B1.OUT_1B
  N7: MD09B1.Enable, Part1.D6_PWM
  N8: MD09B1.MS1, MD09B1.MS2, MD09B1.MS3, Part1.D4
  N9: MD09B1.RESET, MD09B1.SLEEP
  N10: MD09B1.STEP, Part1.D3_PWM
  N11: MD09B1.DIR, Part1.D2
  VDD: MD09B1.VDD, Part1.VIN, R1.pin_0, R3.pin_0, R5.pin_0, R6.pin_0, R9.pin_0, R10.pin_0
  N12: Part1.A0, R5.pin_1, R12.Pin_0
  N13: Part1.A1, R6.pin_1
  N14: Part1.A2, R1.pin_1, R2.Pin_0
  N15: Part1.A3, R3.pin_1, R4.Pin_0
  N16: Part1.A4/SDA, R8.Pin_0, R9.pin_1
  N17: Part1.A5/SCL, R7.Pin_0, R10.pin_1
  N18: S1.leg0, R13.Pin_0
  N19: VCC1.pin1, F1.2

notes:
  capteur photovoltaique 6V

custom parts:
  LC-R121R3P: 12V 1.Ah battery
