# Fritzing sketch SeguiLSol (saved by Fritzing 0.8.7b)
breadboards: 1

parts:
  Part1 = Arduino Mega 2560 (Rev3)
  C2 = Capacitor Polarized [package=panasonic_g]
  M1 = Stepper Motor - Bipolar
  MD09B1 = A4988 Stepper Motor Driver Carrier
  J2 = Screw terminal - 2 pins [package=THT]
  L1 = Photocell (LDR) [package=THT]
  L2 = Photocell (LDR) [package=THT]
  R1 = 10000 Ω Resistor [package=THT]
  R2 = 10000 Ω Resistor [package=THT]

nets (from the breadboard view):
  N1: Part1.A0, L1.pin_0, R1.Pin_1
  N2: Part1.A1, L2.pin_0, R2.Pin_0
  N3: Part1.GND, C2.-, MD09B1.GROUND, J2.pin1, R1.Pin_0, R2.Pin_1
  VIN: Part1.VIN, MD09B1.MS1, MD09B1.MS2, MD09B1.MS3, MD09B1.VDD, L1.pin_1, L2.pin_1
  N4: Part1.D2_PWM, MD09B1.DIR
  N5: Part1.D3_PWM, MD09B1.STEP
  N6: Part1.D6_PWM, MD09B1.Enable
  N7: C2.+, MD09B1.VMOT, J2.pin2
  N8: M1.A, MD09B1.OUT_2A
  N9: M1.C, MD09B1.OUT_2B
  N10: M1.B, MD09B1.OUT_1A
  N11: M1.D, MD09B1.OUT_1B
  N12: MD09B1.RESET, MD09B1.SLEEP

notes:
  motor power supply
  8-35V

custom parts:
  10000 Ω Resistor: A generic resistor (0.25W)
