# Fritzing sketch OSE_Heliostat_Control.022 (saved by Fritzing 0.9.1b)
breadboards: 2

parts:
  C2_100uf = Capacitor Polarized [package=panasonic_g]
  M1 = Stepper Motor - Bipolar
  Arduino = Arduino Uno (Rev3)
  P1_-_PhotoDiode_PdE = S1133 Si Photodiode [package="8mm Ceramic [THT]"]
  R2_1M = Resistor [tolerance=±5% resistance=1M package=THT]
  Power_plug_8V-35V = Power plug
  MD09B2 = A4988 Stepper Motor Driver Carrier
  MD09B3 = A4988 Stepper Motor Driver Carrier
  IC2 = MCP23017 I2C I/O Expander
  M2 = Stepper Motor - Bipolar
  pushEButPin = Momentary Switch [package=ksa_sealed_tac_switch]
  pushWButPin = Momentary Switch [package=ksa_sealed_tac_switch]
  jButPin = Momentary Switch [package=ksa_sealed_tac_switch]
  U1 = POT [package=pot_mammoth]
  R2_1M1 = Resistor [tolerance=±5% resistance=1M package=THT]
  R2_1M2 = Resistor [tolerance=±5% resistance=1M package=THT]
  R2_1M3 = Resistor [tolerance=±5% resistance=1M package=THT]
  R2_1M4 = Resistor [tolerance=±5% resistance=1M package=THT]
  pushCalibrateButPin_10 = Momentary Switch [package=ksa_sealed_tac_switch]
  R2_1M5 = Resistor [tolerance=±5% resistance=1M package=THT]
  endStopPin = Momentary Switch [package=ksa_sealed_tac_switch]
  R2_1M6 = Resistor [tolerance=±5% resistance=1M package=THT]

nets (from the breadboard view):
  N1: C2_100uf.+, Power_plug_8V-35V.VCC, MD09B2.VMOT, MD09B3.VMOT
  GND: C2_100uf.-, Arduino.GND, P1_-_PhotoDiode_PdE.anode, Power_plug_8V-35V.GND, MD09B2.GROUND, MD09B3.GROUND, IC2.VSS, IC2.A0, IC2.A1, IC2.A2, R2_1M1.Pin_1, R2_1M2.Pin_1, R2_1M3.Pin_1, R2_1M4.Pin_1, R2_1M5.Pin_1, R2_1M6.Pin_1
  N2: M1.A, MD09B2.OUT_2A
  N3: M1.C, MD09B2.OUT_2B
  N4: M1.B, MD09B2.OUT_1A
  N5: M1.D, MD09B2.OUT_1B
  N6: Arduino.A0, U1.E, R2_1M1.Pin_0
  N7: Arduino.A3, P1_-_PhotoDiode_PdE.cathode, R2_1M.Pin_1
  N8: Arduino.D8, endStopPin.2, R2_1M6.Pin_0
  N9: Arduino.D10_PWM/SS, pushCalibrateButPin_10.2, R2_1M5.Pin_0
  N10: Arduino.D11_PWM/MOSI, pushEButPin.2, R2_1M4.Pin_0
  N11: Arduino.D12/MISO, pushWButPin.2, R2_1M3.Pin_0
  N12: Arduino.D13/SCK, jButPin.2, R2_1M2.Pin_0
  N13: Arduino.A4/SDA, IC2.SDA
  N14: Arduino.A5/SCL, IC2.SCL
  N15: Arduino.D2, MD09B2.DIR, MD09B3.DIR
  N16: Arduino.D4, MD09B2.MS1, MD09B2.MS2, MD09B2.MS3, MD09B3.MS1, MD09B3.MS2, MD09B3.MS3
  N17: Arduino.D6_PWM, MD09B2.Enable, MD09B3.Enable
  VDD: Arduino.5V, R2_1M.Pin_0, MD09B2.VDD, MD09B3.VDD, IC2.VDD, IC2.RESET, pushEButPin.4, pushWButPin.4, jButPin.4, U1.S, pushCalibrateButPin_10.4, endStopPin.4
  N18: MD09B2.RESET, MD09B2.SLEEP
  N19: MD09B2.STEP, IC2.GPA0
  N20: MD09B3.RESET, MD09B3.SLEEP
  N21: MD09B3.STEP, IC2.GPA1
  N22: MD09B3.OUT_2B, M2.C
  N23: MD09B3.OUT_2A, M2.A
  N24: MD09B3.OUT_1A, M2.B
  N25: MD09B3.OUT_1B, M2.D

custom parts:
  MCP23017 I2C I/O Expander: MCP23017 I2C 16-Channel I/O Expander

// code stored in the sketch: OSE_heliostat_Control0.21.ino
#include <Wire.h> // to control the MCP23017 to control the step on all motors

//**************************************************************
//  Open Souce Écologie - Solar Heliostat controller
//  Name: SeguiLSol25
//  Authors: Andrea Sannuto @ndrsan, Jean Walter , Remi @Remi_R, Cherif 
//  Website: www.osefrance.fr  @OSE_Fr
//  Rev 001 
//  Date 08 April 2015
// features, micro step to follow the sun or heliostat with 1 axis only, as fast as it can to be the most precise.  
// this software is released under the GPL V.3 
// for more recents update, check out the git page: https://github.com/osefrance/SolarConcentrator
// http://bit.ly/1JnwSGd
//**************************************************************


// 5 main functions (to translate in class)
// function 0 = Awake
// function 1 = Find Midpoint / calibration : 
// function 2 = offset mirror 1 and n
// function 3 = Follow the sun, thanks to the offset mirrors and the interrupts of the photoresistors positioned on the edge of the absorber
// function 4 = sleep. go in position to sleep and sleep.

// Status: Function 3 working based on the feedback from the PdE. moves all mirrors at once when PdE reaches the threshold.


// Stepper driver Pin configuration  - set up based on Pololu A4988 driver although also DRV8825 will be integrated in this design.

const int mirrorsQ = 2; // how many mirrors should be controlled. if through the MCP23017 they should be connected incrementally starting from port A0 of MCP23017
int mirrorsQbin = 1; // mirrorsQconversion to consecutive bits rappresenting each single motors
// int stepPin[] = {3, 5, 7}; // 1 high and low cycle makes 1 step of the stepper . minimum 1 uSec per state - "A low-to-high transition on the STEP input sequences the translator and advances the motor one increment. "

int mirrorSel = 1; // index for the mirror selector when using the MCP23017 it will be set to 255 to step on all motors at the same time (set to 0 if used as index for stepPin[] matrix, set to 1 if used as pointer for the MCP23017 port extender

const int dirPin = 2;  // This determines the direction of rotation of the motor. Changes to this input do not take effect until the next STEP rising edge.
const int enablePin = 6; // This input turns on or off all of the FET outputs. When set to a logic high, the outputs are disabled. When set to a logic low, the internal control enables the outputs as required. The translator inputs STEP, DIR, and MSx, as well as the internal sequencing logic, all remain active, independent of ENABLE input state.
const int microStepPin = 4; // This input turns on or off all of the FET outputs. When set to a logic high, the outputs are disabled. When set to a logic low, the internal control enables the outputs as required. The translator inputs STEP, DIR, and MSx, as well as the internal sequencing logic, all remain active, independent of ENABLE input state.


// pin settings
int pushWButPin = 12; // push button to move motors manually to West of 1 (micro)step
int pushEButPin = 11; // push button to move motors manually to Est of 1 (micro)step
int potPin = A0; // potentiometer to set the movement speed of the motor - temporary setting

// Joystick control
int jButPin = 13;
// int jPotxPin = A3;
// int jPotyPin = A1;

// DEBUG MODE 1 on, 0 off. check serial for output of the variables value.
  int debugmode = 0;
// int debugmode = 1;


// Variables
int dir ; // set the direction
int spd ; // set the speed - the higher the slower

// photosensor related variables

const int pdPin[]= {A3} ; // matrix of the photodiodes. - say A3 for the east photodiode (PdE in the schematics) and Ax for the western one (PdW). PdE is the driving photodiode triggering the motors to step if excited. PdW should be mostly used for calibration 
const float pdThreshold = 3 ; // threshold at which the sun hits the photodiode, used for calibration and for heliostat function

void setup() {
  // put your setup code here, to run once:
/*setup of motor's pins connected on the arduino (commented out if you use the MCP23017
for (int a=0; a<mirrorsQ; a++){
  pinMode(stepPin[a], OUTPUT);
}
*/

pinMode(dirPin, OUTPUT);
pinMode(enablePin, OUTPUT);  
pinMode(microStepPin, OUTPUT);  
pinMode(pushWButPin, INPUT);  
pinMode(pushEButPin, INPUT);  

// MCP23017 setup
 Wire.begin(); // wake up I2C bus
// set I/O pins to outputs
 Wire.beginTransmission(0x20);
 Wire.write(0x00); // IODIRA register
 Wire.write(0x00); // set all of port A to outputs
 Wire.endTransmission();
 Wire.beginTransmission(0x20);
 Wire.write(0x01); // IODIRB register
 Wire.write(0x00); // set all of port B to outputs
 Wire.endTransmission();
if (debugmode == 1) { Serial.begin (9600); }
 
for (int a=1; a<= mirrorsQ; a++) { // converts the decimal quantity to binary for later comparison when switching from one motor to the next
   mirrorsQbin= mirrorsQbin * 2;
   }
}

void loop() {
  // put your main code here, to run repeatedly:
digitalWrite(enablePin,LOW ); // set to low to keep the stepper motors engaged in the position. it consumes power but essential in direct drive with environmental perturbances (wind) 
 digitalWrite(microStepPin, HIGH); // microstepping enabled (based on hardware configuration HHH = 1/16th)
// digitalWrite(microStepPin, LOW); // microstepping disabled

// int jButRead = digitalRead(jButPin);

if (digitalRead(jButPin) == HIGH )   { selectMirror(); }

if (digitalRead(pushWButPin) == HIGH ) {
    dir = 0;
    turn(dir,mirrorSel);//moves the mirror(s)
    return ;
    }
if (digitalRead(pushEButPin) == HIGH ) {
    dir = 1;
    turn(dir, mirrorSel);//moves the mirror(s)
    return ;
    }  

float pdreading = readPd (pdPin[0]);
if (pdreading < pdThreshold)  {
    dir = 1;
    turn(dir, 255);//moves all mirrors
    }  
}

void turn (int dirT, int spin){
    digitalWrite(enablePin, LOW);
    digitalWrite(dirPin, dirT);

  spd = map(analogRead (potPin), 1023, 780, 1,3000);
/*  digitalWrite(stepPin[spin], HIGH);
  delayMicroseconds(spd);
  digitalWrite(stepPin[spin], LOW);
  delayMicroseconds(spd);
*/

   // turn A Ports ON based on mirrorSel (Make 1 step)
if (debugmode == 1) {   Serial.println (spin); }
  Wire.beginTransmission(0x20);
       Wire.write(0x12); // GPIOA
       Wire.write(spin); // port A
  Wire.endTransmission();
     // B Ports
  /*   Wire.beginTransmission(0x20);
       Wire.write(0x13); // GPIOB
       Wire.write(a); // port B
     Wire.endTransmission();
  */
  delayMicroseconds(spd);

  // turn OFF A Ports
 
  Wire.beginTransmission(0x20);
       Wire.write(0x12); // GPIOA
       Wire.write(0x00); // port A
  Wire.endTransmission();
     // turn off B Ports
 /*    Wire.beginTransmission(0x20);
       Wire.write(0x13); // GPIOB
       Wire.write(0x00); // port B
     Wire.endTransmission();
  */
 
 delayMicroseconds(spd);
if (debugmode == 1) {   Serial.print ("mirrorSel ; mirrorsQbin");  Serial.print (mirrorSel); Serial.print (" ; "); Serial.println (mirrorsQbin); }

}

 void selectMirror() {
      mirrorSel = mirrorSel *2;
      if (mirrorSel == mirrorsQbin) { mirrorSel = 255;}
      else if (mirrorSel > mirrorsQbin) { mirrorSel = 1;}
      while (digitalRead(jButPin) == HIGH )   {}
    }


float readPd (int photoDiodedPin) // read the photo diode 
{
 int pdRead = analogRead( photoDiodedPin);
 float pdVolt = pdRead / 1024.0 * 5.0;
 if (debugmode == 1)
  {
  Serial.begin (9600);
  Serial.print("inside pdRead : pdVolt ; pdRead = ");
  Serial.print(pdVolt);
  Serial.print(" ; ");
  Serial.print(pdRead);
  Serial.println();
  }
  
return pdVolt;
}



/*
Board	I2C / TWI pins
Uno, Ethernet	A4 (SDA), A5 (SCL)
Mega2560	20 (SDA), 21 (SCL)
Leonardo	2 (SDA), 3 (SCL)
Due	20 (SDA), 21 (SCL), SDA1, SCL1

MCP23017 I2C chip
SCL = 12
SDA = 13

// pins 15~17 to GND, I2C bus address is 0x20
*/
