# Fritzing sketch SeguiLSol_POC_Simple (saved by Fritzing 0.8.7b)
breadboards: 1

parts:
  C2_100uf = Capacitor Polarized [package=panasonic_g]
  M1 = Stepper Motor - Bipolar
  MD09B1 = A4988 Stepper Motor Driver Carrier
  Arduino = Arduino Uno (Rev3)
  P1_-_PhotoDiode_Pdx = S1133 Si Photodiode [package="8mm Ceramic [THT]"]
  R2_1Mohm = Resistor [tolerance=±5% resistance=10k package=THT]
  Power_plug_8V-35V = Power plug

nets (from the schematic view):
  N1: C2_100uf.+, M1.A, M1.B, MD09B1.MS3, MD09B1.VMOT, MD09B1.OUT_2A, MD09B1.OUT_1A, Arduino.D4, Power_plug_8V-35V.VCC
  GND: C2_100uf.-, MD09B1.GROUND#147, Arduino.GND, P1_-_PhotoDiode_Pdx.anode, Power_plug_8V-35V.GND
  N2: M1.C, MD09B1.OUT_2B
  N3: M1.D, MD09B1.OUT_1B
  N4: MD09B1.Enable, Arduino.D6_PWM
  N5: MD09B1.STEP, Arduino.D3_PWM
  N6: MD09B1.DIR, Arduino.D2
  VDD: MD09B1.VDD, Arduino.5V, R2_1Mohm.Pin_0
  N7: Arduino.A2, P1_-_PhotoDiode_Pdx.cathode, R2_1Mohm.Pin_1
