# Fritzing sketch StepperPowerTriacCircuit2 (saved by Fritzing 0.9.1b)

parts:
  U2 = Optocoupler [package=THT]
  Q1 = Basic FET P-Channel [package="TO220 [THT]"]
  R1 = Resistor [tolerance=±5% resistance=220 package="0603 [SMD]"]
  R2 = Resistor [tolerance=±5% resistance=2.2k package="0805 [SMD]"]
  R3 = Resistor [tolerance=±5% resistance=10k package="1206 [SMD]"]
  M1 = Stepper Motor - Bipolar  # not connected
  U3 = Optocoupler [package=THT]
  R5 = Resistor [tolerance=±5% resistance=2.2k package="0805 [SMD]"]
  R6 = Resistor [tolerance=±5% resistance=10k package="1206 [SMD]"]
  Q2 = Basic FET P-Channel [package="TO220 [THT]"]

nets:
  N1: U2.Pin_4, R3.Pin_1
  N2: U2.Pin_6, R2.Pin_0
  N3: Q1.gate, R3.Pin_0
  N4: Q1.drain, R2.Pin_1
  N5: R1.Pin_1, U3.Pin_1
  N6: U3.Pin_2, U3.Pin_3
  N7: U3.Pin_4, U3.Pin_5, R6.Pin_1, Q2.source
  N8: U3.Pin_6, R5.Pin_0
  N9: R5.Pin_1, Q2.drain
  N10: R6.Pin_0, Q2.gate

notes:
  To MCP23017 Pin
  To Arduino Gnd
  To Azimuth Driver Board
  A+
  B+
  A-
  B-
  Warning! The "FETs" in the circuit are actually supposed to be triacs. There were none in the Fritzing part library, so I used the FETs instead.
  Also, the optocoupler in the circuit isn't the one I actually used.
  The part numbers for the optocouplers and triacs are,
  MOC3020M
  2N6073AG
  Both were ordered from Mouser.
  Attributions:
  Original Electronic design source
  www.cerebralmeltdown.com
  by Gabriel
