# Fritzing sketch SeguiLSol 3 (saved by Fritzing 0.9.1b)
breadboards: 1

parts:
  C2 = Capacitor Polarized [package=panasonic_g]
  R5 = Photocell (LDR) [package=THT]
  R6 = Photocell (LDR) [package=THT]
  R7 = Resistor [tolerance=±5% resistance=2.2k package=THT]
  R8 = Resistor [tolerance=±5% resistance=2.2k package=THT]
  R9 = Temperature Sensor (Thermistor) [thermistor_type=NTC package=THT]
  R10 = Temperature Sensor (Thermistor) [thermistor_type=NTC package=THT]
  R11 = Resistor [tolerance=±5% resistance=10k package=THT]
  R12 = Resistor [tolerance=±5% resistance=10k package=THT]
  S1 = Pushbutton [package=THT]
  R13 = Resistor [tolerance=±5% resistance=10k package=THT]
  R14 = Resistor [tolerance=±5% resistance=10 package=THT]
  J3 = Screw terminal - 2 pins [package=THT]
  Composant1 = Arduino Mega 2560 (Rev3)
  MD09B2 = A4988 Stepper Motor Driver Carrier
  MD09B3 = A4988 Stepper Motor Driver Carrier
  MD09B4 = A4988 Stepper Motor Driver Carrier
  M2 = Stepper Motor - Bipolar
  M3 = Stepper Motor - Bipolar
  M4 = Stepper Motor - Bipolar
  LED1 = LED - 5mm [color="Yellow (595nm)" package="5 mm [THT]"]
  LED2 = LED - 5mm [color="Yellow (595nm)" package="5 mm [THT]"]
  S3 = Toggle Switch [package=THT]
  R15 = Resistor [tolerance=±5% resistance=10k package=THT]
  R16 = Resistor [tolerance=±5% resistance=10k package=THT]
  R17 = Resistor [tolerance=±5% resistance=10k package=THT]
  S4 = Toggle Switch [package=THT]
  S5 = Toggle Switch [package=THT]

nets:
  N1: C2.+, J3.pin2, MD09B2.VMOT, MD09B3.VMOT, MD09B4.VMOT
  N2: C2.-, R7.Pin_1, R8.Pin_1, R11.Pin_1, R12.Pin_1, R13.Pin_1, R14.Pin_0, J3.pin1, Composant1.GND, MD09B2.GROUND, MD09B3.GROUND, MD09B4.GROUND, LED1.anode, LED2.anode, R15.Pin_1, R16.Pin_1, R17.Pin_1
  VDD: R5.pin_0, R6.pin_0, R9.pin_0, R10.pin_0, S1.leg1, Composant1.5V, MD09B2.MS1, MD09B2.MS2, MD09B2.MS3, MD09B2.VDD, MD09B3.MS1, MD09B3.MS2, MD09B3.MS3, MD09B3.VDD, MD09B4.MS1, MD09B4.MS2, MD09B4.MS3, MD09B4.VDD, S3.L1, S4.L1, S5.L1
  N3: R5.pin_1, R12.Pin_0, Composant1.A0
  N4: R6.pin_1, R11.Pin_0, Composant1.A1
  N5: R7.Pin_0, R10.pin_1, Composant1.A3
  N6: R8.Pin_0, R9.pin_1, Composant1.A2
  N7: S1.leg0, R13.Pin_0, Composant1.D22
  N8: R14.Pin_1, Composant1.A4
  N9: Composant1.A5, LED1.cathode
  N10: Composant1.A6, LED2.cathode
  N11: Composant1.D24, S3.COM, R15.Pin_0
  N12: Composant1.D26, R16.Pin_0, S4.COM
  N13: Composant1.D28, R17.Pin_0, S5.COM
  N14: Composant1.D31, MD09B2.STEP
  N15: Composant1.D33, MD09B2.DIR
  N16: Composant1.D35, MD09B2.Enable
  N17: Composant1.D37, MD09B3.STEP
  N18: Composant1.D39, MD09B3.DIR
  N19: Composant1.D41, MD09B3.Enable
  N20: Composant1.D43, MD09B4.STEP
  N21: Composant1.D45, MD09B4.DIR
  N22: Composant1.D47, MD09B4.Enable
  N23: MD09B2.RESET, MD09B2.SLEEP
  N24: MD09B2.OUT_2B, M2.C
  N25: MD09B2.OUT_2A, M2.A
  N26: MD09B2.OUT_1A, M2.B
  N27: MD09B2.OUT_1B, M2.D
  N28: MD09B3.RESET, MD09B3.SLEEP
  N29: MD09B3.OUT_2B, M4.C
  N30: MD09B3.OUT_2A, M4.A
  N31: MD09B3.OUT_1A, M4.B
  N32: MD09B3.OUT_1B, M4.D
  N33: MD09B4.RESET, MD09B4.SLEEP
  N34: MD09B4.OUT_2B, M3.C
  N35: MD09B4.OUT_2A, M3.A
  N36: MD09B4.OUT_1A, M3.B
  N37: MD09B4.OUT_1B, M3.D

notes:
  capteur photovoltaique 6V
  motor power supply
  8-35V
